// Logisim project project.circ as structural Verilog: 1 circuit, main circuit main
module main (
  input  X,
  input  Y,
  input  Z
);

  wire and_1_out, and_2_out, and_3_out, and_4_out, and_5_out, and_6_out, not_1_out, not_2_out, not_3_out,
       or_1_out, or_2_out, or_3_out, or_4_out, xor_1_out, xor_2_out;

  not not_1 (not_1_out, Y);
  not not_2 (not_2_out, Z);
  not not_3 (not_3_out, X);
  xor xor_1 (xor_1_out, X, Z);
  or or_1 (or_1_out, not_1_out, not_2_out);
  and and_1 (and_1_out, not_3_out, not_2_out);
  and and_2 (and_2_out, Y, Z);
  and and_3 (and_3_out, X, not_2_out);
  and and_4 (and_4_out, not_3_out, Y);
  and and_5 (and_5_out, or_1_out, not_3_out);
  or or_2 (or_2_out, and_2_out, and_3_out);
  buf and_6 (and_6_out, X);  // AND_Gate
  or or_3 (or_3_out, and_4_out, xor_1_out);
  xor xor_2 (xor_2_out, Y, Z);
  or or_4 (or_4_out, and_6_out, xor_2_out);
  _7_Segment_Display u_7_segment_display_1 (
    .g(or_4_out), .f(or_2_out), .a(or_3_out), .b(and_5_out), .e(xor_1_out), .d(or_3_out), .c(and_1_out));  // open: dp

  // Notes on the sheet:
  //   Z
  //   Y
  //   X
  //   Z'
  //   Y'
  //   X'
  //   X'Z+XZ'
  //   Y'+Z'
  //   X'Y
  //   X'Z'
  //   YZ
  //   XZ'
  //   XY'
  //   Y'Z+YZ'
  //      X'(Y'+Z')
  //   YZ+XZ'
  //   b
  //   e
  //   f
  //   c
  //   d
  //   g
  //   a
endmodule
