// Logisim project sequential (1).circ as structural Verilog: 1 circuit, main circuit main
module main (
  input  in_1,
  input  in_2,
  input  in_3,
  input  in_4
);

  wire and_1_out, and_2_out, and_3_out, and_4_out, and_5_out, and_6_out, and_7_out, and_8_out, and_9_out,
       and_10_out, and_11_out, and_12_out, and_13_out, and_14_out, and_15_out, and_16_out, and_17_out,
       and_18_out, and_19_out, clock_1_out, d_ff_1_q, d_ff_2_q, d_ff_3_q, d_ff_4_q, not_1_out, not_2_out,
       not_3_out, not_4_out, not_5_out, not_6_out, not_7_out, or_1_out, or_2_out, or_3_out, or_4_out,
       or_5_out, or_6_out, or_7_out, or_8_out, or_9_out, or_10_out, or_11_out, or_12_out, xor_1_out,
       xor_2_out;

  not not_1 (not_1_out, d_ff_1_q);
  not not_2 (not_2_out, d_ff_2_q);
  not not_3 (not_3_out, d_ff_3_q);
  not not_4 (not_4_out, d_ff_4_q);
  and and_1 (and_1_out, d_ff_2_q, d_ff_4_q);
  or or_1 (or_1_out, and_1_out, and_2_out);
  and and_2 (and_2_out, d_ff_3_q, d_ff_4_q);
  and and_3 (and_3_out, d_ff_1_q, not_2_out);
  and and_4 (and_4_out, d_ff_2_q, d_ff_3_q);
  and and_5 (and_5_out, d_ff_1_q, d_ff_4_q);
  and and_6 (and_6_out, d_ff_1_q, d_ff_3_q);
  and and_7 (and_7_out, not_3_out, not_4_out);
  and and_8 (and_8_out, not_3_out, d_ff_4_q);
  and and_9 (and_9_out, not_1_out, d_ff_2_q);
  and and_10 (and_10_out, and_9_out, not_3_out);
  and and_11 (and_11_out, not_3_out, not_4_out);
  and and_12 (and_12_out, d_ff_1_q, not_2_out);
  or or_2 (or_2_out, or_1_out, and_3_out);
  or or_3 (or_3_out, and_2_out, and_4_out);
  or or_4 (or_4_out, or_3_out, and_5_out);
  and and_13 (and_13_out, not_2_out, and_7_out);
  or or_5 (or_5_out, and_8_out, and_10_out);
  or or_6 (or_6_out, and_11_out, and_12_out);
  or or_7 (or_7_out, or_4_out, and_6_out);
  or or_8 (or_8_out, or_7_out, and_13_out);
  Clock clock_1 (.out(clock_1_out));
  D_Flip_Flop d_ff_1 (.clk(clock_1_out), .D(or_2_out), .Q(d_ff_1_q), .reset(in_1));  // open: Qn, preset, en
  D_Flip_Flop d_ff_2 (.clk(clock_1_out), .D(or_8_out), .Q(d_ff_2_q), .reset(in_2));  // open: Qn, preset, en
  D_Flip_Flop d_ff_3 (.clk(clock_1_out), .D(or_5_out), .Q(d_ff_3_q), .reset(in_3));  // open: Qn, preset, en
  D_Flip_Flop d_ff_4 (.clk(clock_1_out), .D(or_6_out), .Q(d_ff_4_q), .reset(in_4));  // open: Qn, preset, en
  not not_5 (not_5_out, d_ff_2_q);
  not not_6 (not_6_out, d_ff_3_q);
  not not_7 (not_7_out, d_ff_4_q);
  or or_9 (or_9_out, not_6_out, not_7_out);
  and and_14 (and_14_out, not_5_out, not_7_out);
  and and_15 (and_15_out, d_ff_3_q, d_ff_4_q);
  and and_16 (and_16_out, d_ff_2_q, not_7_out);
  and and_17 (and_17_out, d_ff_2_q, not_6_out);
  xor xor_1 (xor_1_out, d_ff_3_q, d_ff_4_q);
  and and_18 (and_18_out, not_5_out, not_6_out);
  xor xor_2 (xor_2_out, d_ff_2_q, d_ff_4_q);
  or or_10 (or_10_out, and_18_out, xor_2_out);
  and and_19 (and_19_out, or_9_out, not_5_out);
  or or_11 (or_11_out, and_15_out, and_16_out);
  or or_12 (or_12_out, and_17_out, xor_1_out);
  _7_Segment_Display u_7_segment_display_1 (
    .g(or_12_out), .f(or_11_out), .a(or_10_out), .b(and_19_out), .e(xor_2_out), .d(or_10_out), .c(and_14_out));  // open: dp

  // Notes on the sheet:
  //   in
  //   Y
  //   X
  //   z
  //   z
  //   x'
  //   y'
  //   z'
  //          in'
  //   xz
  //   yz
  //   inx'
  //   xy
  //   inz
  //   iny
  //   Y'z
  //   in'x
  //   Y'z'
  //   inx'
  //   yz
  //   x'y'z'
  //      in'xy'
  //   Din
  //   Dy
  //   Dz
  //   Dx
  //   Din(t+1)
  //   Dx(t+1)
  //            Dy(t+1)
  //   Dz(t+1)
  //   x xor z
  //   yz
  //   xz'
  //   xy'
  //   y xor z
  //   x'y
  //   y'+z'
  //   x'z'
  //   e
  //        x'(y'+z')
  //   x'
  //   a=d
  //   b
  //   c
  //   f
  //   g
  //       d
endmodule
